# Fritzing sketch push_button_trigger_led (saved by Fritzing 0.9.3b)
breadboards: 1

parts:
  Raspberry_Pi_1 = Raspberry Pi 3 [part_number=RPI-3-V1.2]
  R1 = Resistor [tolerance=±5% resistance=330 package=THT]
  LED1 = LED - 5mm [color="White (4500K)" package="5 mm [THT]"]
  Q1 = PNP-Transistor [package="TO92 [THT]"]
  S1 = Pushbutton [package="[THT]"]

nets:
  N1: Raspberry_Pi_1.3v3, S1.Pin_3, S1.Pin_4
  N2: Raspberry_Pi_1.GIPO17, Q1.B
  N3: Raspberry_Pi_1.GIPO27, S1.Pin_1, S1.Pin_2
  N4: Raspberry_Pi_1.5V, R1.Pin_0, Q1.E
  N5: R1.Pin_1, LED1.anode
  N6: LED1.cathode, Q1.C
