# Fritzing sketch temperature_triggered_motor (saved by Fritzing 0.9.3b)
breadboards: 1

parts:
  Raspberry_Pi_1 = Raspberry Pi 3 [part_number=RPI-3-V1.2]
  Part1 = Humidity Temperature Sensor SHT15  # not connected
  Q1 = PNP-Transistor [package="TO92 [THT]"]
  Q2 = PNP-Transistor [package="TO92 [THT]"]
  R1 = Resistor [tolerance=±5% resistance=220 package="0603 [SMD]"]
  R2 = Resistor [tolerance=±5% resistance=220 package="0603 [SMD]"]
  LED1 = smd LED [color="Red (633nm)" package="0603 [SMD]"]
  LED2 = smd LED [color="Blue (470nm)" package="0603 [SMD]"]

nets:
  N1: Raspberry_Pi_1.GND, Q1.E, Q2.E
  N2: Raspberry_Pi_1.GPIO17, Q2.B
  N3: Raspberry_Pi_1.GPIO27, Q1.B
  N4: Raspberry_Pi_1.5V, R1.Pin_1, R2.Pin_1
  N5: Q1.C, LED2.cathode
  N6: Q2.C, LED1.cathode
  N7: R1.Pin_0, LED1.anode
  N8: R2.Pin_0, LED2.anode
